# Fritzing sketch project (saved by Fritzing 0.8.7b)
breadboards: 1

parts:
  Part1 = Arduino Mega ADK (Rev3)
  Part2 = Arduino Uno (Rev3)
  R1 = Photocell (LDR) [package=THT]
  DFPlayer_Mini1 = DFPlayer MINI [package="DIP (Dual Inline) [THT]"]
  SP1 = SPEAKER [package=pcb_mount_speaker]
  R2 = Resistor [package="2512 [SMD]"]
  VCC1 = Battery
  M1 = DC Motor
  M2 = DC Motor
  L298N1 = L298N DC motor driver
  Part3 = Thumb Joystick
  Part4 = 2.4 Touchscreen TFT Breakout w:MicroSD
  7_Segment1 = 7 Segment Display
  R3 = Resistor [tolerance=±5% resistance=220 package=THT]
  Part5 = KY-033 Tracing Black White Line Hunting Sensor Module For Arduino
  Part6 = KY-033 Tracing Black White Line Hunting Sensor Module For Arduino
  J1 = Piezo Speaker
  LED1 = LED - 5mm [color="Red (633nm)" package="5 mm [THT]"]
  LED2 = LED - 5mm [color="Red (633nm)" package="5 mm [THT]"]
  R4 = Resistor [package="2512 [SMD]"]

nets:
  N1: Part1.A0, Part3.VERT
  N2: Part1.A1, Part3.HORZ
  N3: Part1.A2, R1.pin_1, R2.Pin_0
  N4: Part1.D21/SCL, Part2.A5/SCL, Part4.C/D, Part4.CLK
  N5: Part1.D20/SDA, Part2.A4/SDA, Part4.WR, Part4.WR_DC
  N6: Part1.D19/RX1, DFPlayer_Mini1.TX
  N7: Part1.D18/TX1, R4.Pin_1
  N8: Part1.D12_PWM, J1.pin2
  N9: Part1.D11_PWM, LED1.anode
  N10: Part1.D10_PWM, LED2.anode
  N11: Part1.D9_PWM, L298N1.ENA
  N12: Part1.D8_PWM, L298N1.IN1
  5V: Part1.5V, Part1.VIN, DFPlayer_Mini1.VCC, R2.Pin_1, L298N1.5V, Part3.VCC, R3.Pin_0, Part5.V+
  GND: Part1.GND, Part2.GND, R1.pin_0, DFPlayer_Mini1.GND#6, VCC1.-, L298N1.GND, Part3.GND, Part4.RST, Part5.GND, J1.pin1, LED1.cathode, LED2.cathode
  N13: Part1.D2_PWM, Part5.S
  N14: Part1.D3_PWM, Part6.S
  N15: Part1.D4_PWM, L298N1.ENB
  N16: Part1.D5_PWM, L298N1.IN4
  N17: Part1.D6_PWM, L298N1.IN3
  N18: Part1.D7_PWM, L298N1.IN2
  N19: Part1.D22, 7_Segment1.Segment_G
  N20: Part1.D23, 7_Segment1.Segment_F
  N21: Part1.D24, 7_Segment1.Segment_A
  N22: Part1.D25, 7_Segment1.Segment_B
  N23: Part1.D26, 7_Segment1.Segment_E
  N24: Part1.D27, 7_Segment1.Segment_D
  N25: Part1.D28, 7_Segment1.Segment_C
  N26: Part2.D8, Part4.D0
  N27: Part2.D9_PWM, Part4.Y-
  N28: Part2.D10_PWM/SS, Part4.X-
  N29: Part2.D11_PWM/MOSI, Part4.Y+
  N30: Part2.D12/MISO, Part4.X+
  N31: Part2.D13/SCK, Part4.LITE
  N32: Part2.AREF, Part4.RD
  VIN: Part2.VIN, VCC1.+, L298N1.12V
  N33: DFPlayer_Mini1.RX, R4.Pin_0
  N34: DFPlayer_Mini1.SPK1, SP1.-
  N35: DFPlayer_Mini1.SPK2, SP1.+
  N36: M1.pin_1, L298N1.OUT4
  N37: M1.pin_2, L298N1.OUT3
  N38: M2.pin_1, L298N1.OUT2
  N39: M2.pin_2, L298N1.OUT1
  N40: 7_Segment1.common_anode, R3.Pin_1

custom parts:
  DFPlayer MINI: MP3 module by DFRobot.com for playing Music from an SD-Card. Supports WAV and MP3 files.
  L298N DC motor driver: 2x DC motor driver with 78M05 positive voltage regulator (7..35 V) L298N: max 46 V, 2 A Set 5 V Enable jumper to enable 5 V regultor (needed for the L298N) and +5 V output at screw terminal or supply external +5 V at screw terminal Set ENA and/or ENB to +5 V to enable motor permanently or supply ENA and/or ENB with PWM signal IN1 and IN2 set rotation directory for motor A (OUT1/OUT2) IN2 and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
  2.4 Touchscreen TFT Breakout w:MicroSD: Add some jazz & pizzazz to your project with a color touchscreen LCD. This TFT display is 2.4" diagonal with a bright (4 white-LED) backlight and it's colorful! 240x320 pixels with individual RGB pixel control, this has way more resolution than a black and white 128x64 display. As a bonus, this display has a resistive touchscreen attached to it already, so you can detect finger presses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
  KY-033 Tracing Black White Line Hunting Sensor Module For Arduino: Tracing Black White Line Hunting Sensor Module For Arduino Description: This is KY-033 tracking sensor. The KY-033 measures the intensity of infrared radiation and delivers it as an analog output voltage. Features: Operating voltage: 2.5 - 12V(cannot over12V) working current: 18mA-20mA at 5V Enhanced accuracy Documents: http://www.vishay.com/docs/83760/tcrt5000.pdf
